// Digital circuit FlipFlopD.dig as structural Verilog
module FlipFlopD (
  input  D,
  input  Cl,
  input  En,
  output Q,
  output nQ
);

  wire not_1_out;

  not not_1 (not_1_out, D);
  and and_1 (Q, D, En, Cl);
  and and_2 (nQ, Cl, En, not_1_out);
endmodule
