// Digital circuit RegB.dig as structural Verilog
module RegB (
  input  Clk,
  input  Lb,
  input  E1,
  input  E2,
  input  E3,
  input  E4,
  input  E5,
  input  E6,
  input  E7,
  input  E8,
  output S1,
  output S2,
  output S3,
  output S4,
  output S5,
  output S6,
  output S7,
  output S8
);

  wire not_1_out;

  not not_1 (not_1_out, Lb);
  FlipFlopD flipflopd_1 (.D(E1), .Cl(Clk), .En(not_1_out), .Q(S1));  // open: nQ
  FlipFlopD flipflopd_2 (.D(E5), .Cl(Clk), .En(not_1_out), .Q(S5));  // open: nQ
  FlipFlopD flipflopd_3 (.D(E2), .Cl(Clk), .En(not_1_out), .Q(S2));  // open: nQ
  FlipFlopD flipflopd_4 (.D(E6), .Cl(Clk), .En(not_1_out), .Q(S6));  // open: nQ
  FlipFlopD flipflopd_5 (.D(E3), .Cl(Clk), .En(not_1_out), .Q(S3));  // open: nQ
  FlipFlopD flipflopd_6 (.D(E7), .Cl(Clk), .En(not_1_out), .Q(S7));  // open: nQ
  FlipFlopD flipflopd_7 (.D(E4), .Cl(Clk), .En(not_1_out), .Q(S4));  // open: nQ
  FlipFlopD flipflopd_8 (.D(E8), .Cl(Clk), .En(not_1_out), .Q(S8));  // open: nQ
endmodule
