// Digital circuit SAP-1.dig as structural Verilog
module SAP_1 (
  input  [7:0] in_1,
  input  in_2,
  input  [7:0] in_3,
  input  in_4,
  input  in_5,
  input  [3:0] in_6,
  input  clk,
  input  in_8,
  input  in_9
);

  wire [3:0] counter_1_out, register_1_q;
  wire [7:0] register_2_q, register_3_q;

  Register #(.Bits(4)) register_1 (.D(counter_1_out), .C(clk), .en(in_9), .Q(register_1_q));
  Decoder decoder_1 (.sel(register_1_q[0]));  // open: out_0, out_1
  Counter #(.Bits(4)) counter_1 (.en(in_6[0]), .C(clk), .clr(in_8), .out(counter_1_out));  // open: ovf
  Register #(.Bits(8)) register_2 (.D(in_3), .C(clk), .en(in_4), .Q(register_2_q));
  Register #(.Bits(8)) register_3 (.D(in_1), .C(clk), .en(in_2), .Q(register_3_q));
  Add #(.Bits(8)) add_1 (.a(register_2_q), .b(register_3_q), .c_i(in_5));  // open: s, c_o
  // Pins of 1 and 4 bits meet at in_6
  // Pins of 1 and 4 bits meet at register_1_q
endmodule
