// Digital circuit SAP_Atualizacao.dig as structural Verilog
module SAP_Atualizacao (
  input  in_1,
  input  clk
);

  wire d_ff_1_q, d_ff_2_q, d_ff_3_q, d_ff_4_q, jk_ff_1_nq, jk_ff_1_q, jk_ff_2_nq, jk_ff_2_q, jk_ff_3_nq,
       jk_ff_3_q, jk_ff_4_nq;

  JK_FF jk_ff_1 (.J(in_1), .C(clk), .K(in_1), .Q(jk_ff_1_q), .nQ(jk_ff_1_nq));
  D_FF d_ff_1 (.D(jk_ff_4_nq), .C(clk), .Q(d_ff_1_q));  // open: nQ
  JK_FF jk_ff_2 (.J(in_1), .C(jk_ff_1_q), .K(in_1), .Q(jk_ff_2_q), .nQ(jk_ff_2_nq));
  LED led_1 (.in(d_ff_1_q));
  D_FF d_ff_2 (.D(jk_ff_3_nq), .C(clk), .Q(d_ff_2_q));  // open: nQ
  JK_FF jk_ff_3 (.J(in_1), .C(jk_ff_2_q), .K(in_1), .Q(jk_ff_3_q), .nQ(jk_ff_3_nq));
  LED led_2 (.in(d_ff_2_q));
  D_FF d_ff_3 (.D(jk_ff_2_nq), .C(clk), .Q(d_ff_3_q));  // open: nQ
  JK_FF jk_ff_4 (.J(in_1), .C(jk_ff_3_q), .K(in_1), .nQ(jk_ff_4_nq));  // open: Q
  LED led_3 (.in(d_ff_3_q));
  D_FF d_ff_4 (.D(jk_ff_1_nq), .C(clk), .Q(d_ff_4_q));  // open: nQ
  LED led_4 (.in(d_ff_4_q));
endmodule
