// Digital circuit celulaRAM.dig as structural Verilog
module celulaRAM (
  input  E1,
  input  E2,
  input  E3,
  input  E4,
  input  E5,
  input  E6,
  input  E7,
  input  E8,
  input  Clk,
  input  En,
  input  Clr,
  output S1,
  output S2,
  output S3,
  output S4,
  output S5,
  output S6,
  output S7,
  output S8
);

  wire flipflopd_1_q, flipflopd_2_q, flipflopd_3_q, flipflopd_4_q, flipflopd_5_q, flipflopd_6_q,
       flipflopd_7_q, flipflopd_8_q, not_1_out;

  not not_1 (not_1_out, Clr);
  FlipFlopD flipflopd_1 (.D(E1), .Cl(Clk), .En(En), .Q(flipflopd_1_q));  // open: nQ
  and and_1 (S1, flipflopd_1_q, not_1_out);
  FlipFlopD flipflopd_2 (.D(E2), .Cl(Clk), .En(En), .Q(flipflopd_2_q));  // open: nQ
  FlipFlopD flipflopd_3 (.D(E3), .Cl(Clk), .En(En), .Q(flipflopd_3_q));  // open: nQ
  and and_2 (S2, flipflopd_2_q, not_1_out);
  and and_3 (S3, flipflopd_3_q, not_1_out);
  FlipFlopD flipflopd_4 (.D(E4), .Cl(Clk), .En(En), .Q(flipflopd_4_q));  // open: nQ
  FlipFlopD flipflopd_5 (.D(E5), .Cl(Clk), .En(En), .Q(flipflopd_5_q));  // open: nQ
  and and_4 (S4, flipflopd_4_q, not_1_out);
  and and_5 (S5, flipflopd_5_q, not_1_out);
  FlipFlopD flipflopd_6 (.D(E6), .Cl(Clk), .En(En), .Q(flipflopd_6_q));  // open: nQ
  FlipFlopD flipflopd_7 (.D(E7), .Cl(Clk), .En(En), .Q(flipflopd_7_q));  // open: nQ
  and and_6 (S6, flipflopd_6_q, not_1_out);
  and and_7 (S7, flipflopd_7_q, not_1_out);
  FlipFlopD flipflopd_8 (.D(E8), .Cl(Clk), .En(En), .Q(flipflopd_8_q));  // open: nQ
  and and_8 (S8, flipflopd_8_q, not_1_out);
endmodule
