// Digital circuit contadorAssincrono.dig as structural Verilog
module contadorAssincrono (
  input  Clr,
  input  Clk,
  input  Enable,
  output S1,
  output S2,
  output S3,
  output S4
);

  FlipFlopMestEscrPreClear flipflopmestescrpreclear_1 (
    .J(Clr), .K(Clr), .CLK(Clk), .Preset(Clr), .Clr(Enable), .Q(S1));  // open: nQ
  FlipFlopMestEscrPreClear flipflopmestescrpreclear_2 (
    .J(Clr), .K(Clr), .CLK(S1), .Preset(Clr), .Clr(Enable), .Q(S2));  // open: nQ
  FlipFlopMestEscrPreClear flipflopmestescrpreclear_3 (
    .J(Clr), .K(Clr), .CLK(S2), .Preset(Clr), .Clr(Enable), .Q(S3));  // open: nQ
  FlipFlopMestEscrPreClear flipflopmestescrpreclear_4 (
    .J(Clr), .K(Clr), .CLK(S3), .Preset(Clr), .Clr(Enable), .Q(S4));  // open: nQ
endmodule
