// Digital circuit decoder4BITS.dig as structural Verilog
module decoder4BITS (
  input  A,
  input  B,
  input  C,
  input  D,
  output _0,
  output _1,
  output _2,
  output _3,
  output _4,
  output _5,
  output _6,
  output _7,
  output _8,
  output _9,
  output _10,
  output _11,
  output _12,
  output _13,
  output _14,
  output _15
);

  wire not_1_out, not_2_out, not_3_out, not_4_out, not_5_out, not_6_out, not_7_out, not_8_out, not_9_out,
       not_10_out;

  not not_1 (not_1_out, A);
  not not_2 (not_2_out, B);
  not not_3 (not_3_out, C);
  not not_4 (not_4_out, C);
  not not_5 (not_5_out, C);
  not not_6 (not_6_out, C);
  not not_7 (not_7_out, C);
  not not_8 (not_8_out, C);
  not not_9 (not_9_out, C);
  not not_10 (not_10_out, D);
  and and_1 (_0, not_1_out, not_2_out, not_3_out, not_10_out);
  and and_2 (_1, not_1_out, not_2_out, not_3_out, D);
  and and_3 (_2, not_1_out, not_2_out, C, not_10_out);
  and and_4 (_3, not_1_out, not_2_out, C, D);
  and and_5 (_4, not_1_out, B, not_4_out, not_10_out);
  and and_6 (_5, not_1_out, B, not_5_out, D);
  and and_7 (_6, not_1_out, B, C, not_10_out);
  and and_8 (_7, not_1_out, B, C, D);
  and and_9 (_8, A, not_2_out, not_6_out, not_10_out);
  and and_10 (_9, A, not_2_out, not_7_out, D);
  and and_11 (_10, A, not_2_out, C, not_10_out);
  and and_12 (_11, A, not_2_out, C, D);
  and and_13 (_12, A, B, not_8_out, not_10_out);
  and and_14 (_13, A, B, not_9_out, D);
  and and_15 (_14, A, B, C, not_10_out);
  and and_16 (_15, A, B, C, D);
endmodule
