// Digital circuit main2.dig as structural Verilog
module main2 (
  input  in_1,
  input  clk,
  input  in_3
);

  wire celularam_1_p1, celularam_2_p1, celularam_3_p1, celularam_4_p1, celularam_5_p1, celularam_6_p1,
       celularam_7_p1, celularam_8_p1, celularam_9_p1, celularam_10_p1, celularam_11_p1, celularam_12_p1,
       celularam_13_p1, celularam_14_p1, celularam_15_p1, celularam_16_p1, contadorassincrono_1_s1,
       contadorassincrono_1_s2, contadorassincrono_1_s3, contadorassincrono_1_s4;

  // celulaRAM celularam_1: pin names not known; wires that end beside it: celularam_1_p1
  // celulaRAM celularam_2: pin names not known; wires that end beside it: celularam_2_p1
  // celulaRAM celularam_3: pin names not known; wires that end beside it: celularam_3_p1
  // celulaRAM celularam_4: pin names not known; wires that end beside it: celularam_4_p1
  // celulaRAM celularam_5: pin names not known; wires that end beside it: celularam_5_p1
  // celulaRAM celularam_6: pin names not known; wires that end beside it: celularam_6_p1
  // celulaRAM celularam_7: pin names not known; wires that end beside it: celularam_7_p1
  // celulaRAM celularam_8: pin names not known; wires that end beside it: celularam_8_p1
  // celulaRAM celularam_9: pin names not known; wires that end beside it: celularam_9_p1
  // celulaRAM celularam_10: pin names not known; wires that end beside it: celularam_10_p1
  // celulaRAM celularam_11: pin names not known; wires that end beside it: celularam_11_p1
  // celulaRAM celularam_12: pin names not known; wires that end beside it: celularam_12_p1
  // celulaRAM celularam_13: pin names not known; wires that end beside it: celularam_13_p1
  // celulaRAM celularam_14: pin names not known; wires that end beside it: celularam_14_p1
  // celulaRAM celularam_15: pin names not known; wires that end beside it: celularam_15_p1
  // celulaRAM celularam_16: pin names not known; wires that end beside it: celularam_16_p1
  decoder4BITS decoder4bits_1 (
    .A(contadorassincrono_1_s4), .B(contadorassincrono_1_s3), .C(contadorassincrono_1_s2),
    .D(contadorassincrono_1_s1), ._0(celularam_1_p1), ._1(celularam_5_p1), ._2(celularam_9_p1),
    ._3(celularam_13_p1), ._4(celularam_2_p1), ._5(celularam_6_p1), ._6(celularam_10_p1),
    ._7(celularam_14_p1), ._8(celularam_3_p1), ._9(celularam_7_p1), ._10(celularam_11_p1),
    ._11(celularam_15_p1), ._12(celularam_4_p1), ._13(celularam_8_p1), ._14(celularam_12_p1),
    ._15(celularam_16_p1));
  contadorAssincrono contadorassincrono_1 (
    .Clr(in_1), .Clk(clk), .Enable(in_3), .S1(contadorassincrono_1_s1), .S2(contadorassincrono_1_s2),
    .S3(contadorassincrono_1_s3), .S4(contadorassincrono_1_s4));
endmodule
