// Digital circuit regEnderec.dig as structural Verilog
module regEnderec (
  input  E1,
  input  E2,
  input  E3,
  input  E4,
  input  clk,
  input  En,
  output S1,
  output S2,
  output S3,
  output S4
);

  FlipFlopD flipflopd_1 (.D(E1), .Cl(clk), .En(En), .Q(S1));  // open: nQ
  FlipFlopD flipflopd_2 (.D(E2), .Cl(clk), .En(En), .Q(S2));  // open: nQ
  FlipFlopD flipflopd_3 (.D(E3), .Cl(clk), .En(En), .Q(S3));  // open: nQ
  FlipFlopD flipflopd_4 (.D(E4), .Cl(clk), .En(En), .Q(S4));  // open: nQ
endmodule
